# Fritzing sketch Sketch 2 (saved by Fritzing 0.9.3b)

parts:
  U1 = ESP8266 NodeMCU LoLin module
  AMS1 = AMS1777 5V regulator module
  VCC1 = Battery
  DS1 = DS18B20 1-Wire Temperature Sensor Probe
  R1 = Resistor [tolerance=±5% resistance=4.7k package="1206 [SMD]"]  # not connected
  LED1 = smd LED [color="Green (555nm)" package="1206 [SMD]"]
  LED2 = smd LED [color="Red (633nm)" package="1206 [SMD]"]
  R2 = Resistor [tolerance=±5% resistance=220 package="2512 [SMD]"]
  R3 = Resistor [tolerance=±5% resistance=220 package="2512 [SMD]"]

nets:
  N1: U1.D2, DS1.DQ
  3V3: U1.3V3, DS1.VDD
  GND: U1.GND, AMS1.GND-_(output), DS1.GND
  N2: U1.D7, LED1.anode
  N3: U1.D8, LED2.anode
  N4: U1.Vin, AMS1.VOUT+
  N5: AMS1.VIN+, VCC1.+
  N6: AMS1.GND-_(input), VCC1.-
  N7: R2.Pin_1, R3.Pin_1

custom parts:
  ESP8266 NodeMCU LoLin module: ESP8266 based NodeMCU
  AMS1777 5V regulator module: AMS1777 5V regulator module source : https://github.com/ShenTengTu/fritzing_parts/tree/master/voltage%20regulator/AMS1117_5V_regulator_module
  Battery: Your standard 2x 18650 battery pack (7.4 Volts)
